# Fritzing sketch schematic (saved by Fritzing 0.7.12b)

parts:
  Arduino1 = Arduino
  R4 = Resistor [tolerance=±5% resistance=2.2k package=THT]
  R5 = Resistor [tolerance=±5% resistance=2.2k package=THT]
  R6 = Resistor [tolerance=±5% resistance=2.2k package=THT]
  R7 = Resistor [tolerance=±5% resistance=2.2k package=THT]
  R8 = Resistor [tolerance=±5% resistance=2.2k package=THT]
  R1 = Resistor [tolerance=±5% resistance=10k package=THT]

nets:
  N1: Arduino1.D7, R1.Pin_1
  N2: Arduino1.GND, R6.Pin_0
  N3: Arduino1.A0, R7.Pin_1, R1.Pin_0
  N4: R4.Pin_0, R5.Pin_1
  N5: R4.Pin_1, R8.Pin_0
  N6: R5.Pin_0, R6.Pin_1
  N7: R7.Pin_0, R8.Pin_1

notes:
  <--- Sensor will be submerged in water up to this point
